// Logisim project processor.circ as structural Verilog: 5 circuits, main circuit main
module main (
  input  Clear
);

  wire clk, clr, cu_1_cpu_halt, enableIR, enPC, enRWrite, memEnable, memLoadStore, not_1_out, Reset_out,
       selectMuxA, selectMuxB, selectMuxINC, selectMuxPC, selectMuxY;
  wire [1:0] ALU_Out;
  wire [4:0] selectRA, selectRB, selectRC;
  wire [7:0] ALU_Control_In;
  wire [15:0] adder_1_out, bit_extender_1_out, bit_extender_2_out, multiplexer_3_out, multiplexer_4_out, PC;
  wire [15:9] cu_1_output_signals;
  wire [31:0] alu_1_out, Immediate, IR_q, IRin, multiplexer_1_out, multiplexer_2_out, RA_2_q, RB_2_q,
       registerfile_1_outputra, registerfile_1_outputrb, RMout, RY_q, RZ;

  // Probe on RY_q
  RegisterFile registerfile_1 (
    .selectRA(selectRA), .clock(clk), .selectRB(selectRB), .clear(clr), .selectRC(selectRC),
    .enWrite(enRWrite), .inputRC(RY_q), .outputRA(registerfile_1_outputra), .outputRB(registerfile_1_outputrb));
  // Probe on registerfile_1_outputra
  Register #(.width(32)) RA_2 (.D(registerfile_1_outputra), .en(1'b1), .Q(RA_2_q), .clk(clk), .clr(clr));
  // Probe on ALU_Out
  ALU alu_1 (
    .inA(RA_2_q), .inB(multiplexer_1_out), .out(alu_1_out), .ALU_Control_In(ALU_Control_In),
    .ALU_Control_Out(ALU_Out));
  // Probe on alu_1_out
  // Probe on registerfile_1_outputrb
  Register #(.width(32)) RB_2 (.D(registerfile_1_outputrb), .en(1'b1), .Q(RB_2_q), .clk(clk), .clr(clr));
  Multiplexer #(.width(32), .enable("false")) multiplexer_1 (
    .in0(RB_2_q), .in1(Immediate), .out(multiplexer_1_out), .sel(selectMuxB));
  Register #(.width(32)) u_RZ (.D(alu_1_out), .en(1'b1), .Q(RZ), .clk(clk), .clr(clr));
  Multiplexer #(.width(32), .enable("false")) multiplexer_2 (
    .in0(RZ), .in1(IRin), .out(multiplexer_2_out), .sel(selectMuxY));
  // Probe on RZ
  // Probe on RY_q
  Register #(.width(32)) RY (.D(multiplexer_2_out), .en(1'b1), .Q(RY_q), .clk(clk), .clr(clr));
  Register #(.width(32)) RM (.D(RB_2_q), .en(1'b1), .Q(RMout), .clk(clk), .clr(clr));
  Bit_Extender #(.in_width(32)) bit_extender_1 (.in(RZ), .out(bit_extender_1_out));
  Multiplexer #(.width(16), .enable("false")) multiplexer_3 (
    .in0(bit_extender_1_out), .in1(adder_1_out), .out(multiplexer_3_out), .sel(selectMuxPC));
  Register #(.width(16)) u_PC (.D(multiplexer_3_out), .en(enPC), .Q(PC), .clk(clk), .clr(clr));
  or or_1 (clr, Clear, Reset_out);
  Button Reset (.out(Reset_out));
  // Probe on PC
  CU cu_1 (
    .IR(IR_q), .Clock(clk), .Immediate(Immediate),
    .Output_Signals({selectRC, selectRB, selectRA, selectMuxY, cu_1_output_signals, enPC, enableIR, enRWrite, selectMuxPC, selectMuxINC, selectMuxB, selectMuxA, memLoadStore, memEnable}),
    .Clear(clr), .CPU_Halt(cu_1_cpu_halt), .ALU_Control(ALU_Control_In), .ALU_Control_Out(ALU_Out));
  Register #(.width(32)) IR (.D(IRin), .en(enableIR), .Q(IR_q), .clk(clk), .clr(clr));
  Bit_Extender #(.in_width(32)) bit_extender_2 (.in(RZ), .out(bit_extender_2_out));
  Multiplexer #(.width(16), .enable("false")) multiplexer_4 (
    .in0(bit_extender_2_out), .in1(PC), .out(multiplexer_4_out), .sel(selectMuxA));
  Adder #(.width(16)) adder_1 (.a(PC), .b(16'h1), .out(adder_1_out));  // open: cin, cout
  // Probe on multiplexer_4_out
  not not_1 (not_1_out, memLoadStore);
  // Probe on IR_q
  // Probe on IRin
  RAM #(.addrWidth(16), .dataWidth(32), .bus("separate")) ram_1 (
    .addr(multiplexer_4_out), .din(RMout), .data(IRin), .str(not_1_out), .sel(memEnable), .clk(clk),
    .ld(memLoadStore), .clr(1'b0));
  LED CPU_Status__Running_Halt (.in(cu_1_cpu_halt));
  // Probe on selectRA
  // Probe on selectRB
  // Probe on selectRC

  // Other names for the same wires on the sheet: memData[31:0] = IRin

  // Notes on the sheet:
  //   OF-EX-RW Unit
  //   Instruction Fetch Unit
  //   MA Unit
endmodule

// Register file
module RegisterFile (
  input  clock,
  input  [4:0] selectRA,
  input  clear,
  input  [4:0] selectRB,
  input  [31:0] inputRC,
  input  enWrite,
  input  [4:0] selectRC,
  output [31:0] outputRB,
  output [31:0] outputRA
);

  wire enR0, enR1, enR2, enR3, enR4, enR5, enR6, enR7, enR8, enR9, enR10, enR11, enR12, enR13, enR14, enR15,
       enR16, enR17, enR18, enR19, enR20, enR21, enR22, enR23, enR24, enR25, enR26, enR27, enR28, enR29,
       enR30, enR31;
  wire [31:0] R0out, R1out, R2out, R3out, R4out, R5out, R6out, R7out, R8out, R9out, R10out, R11out, R12out,
       R13out, R14out, R15out, R16out, R17out, R18out, R19out, R20out, R21out, R22out, R23out, R24out,
       R25out, R26out, R27out, R28out, R29out, R30out, R31out;

  // Probe on inputRC
  // Probe on inputRC
  // Probe on inputRC
  // Probe on inputRC
  Demultiplexer #(.select(5), .enable("false")) demultiplexer_1 (
    .out0(enR0), .out1(enR1), .out2(enR2), .out3(enR3), .out4(enR4), .out5(enR5), .out6(enR6), .out7(enR7),
    .out8(enR8), .out9(enR9), .out10(enR10), .out11(enR11), .out12(enR12), .out13(enR13), .out14(enR14),
    .out15(enR15), .out16(enR16), .out17(enR17), .out18(enR18), .out19(enR19), .out20(enR20), .out21(enR21),
    .out22(enR22), .out23(enR23), .out24(enR24), .out25(enR25), .out26(enR26), .out27(enR27), .out28(enR28),
    .out29(enR29), .out30(enR30), .out31(enR31), .in(enWrite), .sel(selectRC));
  // Probe on R0out
  // Probe on R2out
  // Probe on R4out
  // Probe on R6out
  // Probe on R8out
  // Probe on R10out
  // Probe on R12out
  // Probe on R14out
  // Probe on R0out
  Register #(.width(32)) register_1 (.D(inputRC), .en(enR0), .Q(R0out), .clk(clock), .clr(clear));
  // Probe on R8out
  Register #(.width(32)) register_2 (.D(inputRC), .en(enR8), .Q(R8out), .clk(clock), .clr(clear));
  // Probe on R16out
  Register #(.width(32)) register_3 (.D(inputRC), .en(enR16), .Q(R16out), .clk(clock), .clr(clear));
  // Probe on R24out
  Register #(.width(32)) register_4 (.D(inputRC), .en(enR24), .Q(R24out), .clk(clock), .clr(clear));
  // Probe on R1out
  // Probe on R3out
  // Probe on R5out
  // Probe on R7out
  // Probe on R9out
  // Probe on R11out
  // Probe on R13out
  // Probe on R15out
  // Probe on inputRC
  // Probe on inputRC
  // Probe on inputRC
  // Probe on inputRC
  // Probe on R1out
  Register #(.width(32)) register_5 (.D(inputRC), .en(enR1), .Q(R1out), .clk(clock), .clr(clear));
  // Probe on R9out
  Register #(.width(32)) register_6 (.D(inputRC), .en(enR9), .Q(R9out), .clk(clock), .clr(clear));
  Register #(.width(32)) register_7 (.D(inputRC), .en(enR17), .Q(R17out), .clk(clock), .clr(clear));
  Register #(.width(32)) register_8 (.D(inputRC), .en(enR25), .Q(R25out), .clk(clock), .clr(clear));
  // Probe on R17out
  // Probe on R25out
  // Probe on R16out
  // Probe on R18out
  // Probe on R20out
  // Probe on R22out
  // Probe on R24out
  // Probe on R26out
  // Probe on R28out
  // Probe on R30out
  // Probe on inputRC
  Register #(.width(32)) register_9 (.D(inputRC), .en(enR2), .Q(R2out), .clk(clock), .clr(clear));
  // Probe on inputRC
  Register #(.width(32)) register_10 (.D(inputRC), .en(enR10), .Q(R10out), .clk(clock), .clr(clear));
  // Probe on inputRC
  // Probe on inputRC
  Multiplexer #(.select(5), .width(32), .enable("false")) multiplexer_1 (
    .in0(R0out), .in1(R1out), .in2(R2out), .in3(R3out), .in4(R4out), .in5(R5out), .in6(R6out), .in7(R7out),
    .in8(R8out), .in9(R9out), .in10(R10out), .in11(R11out), .in12(R12out), .in13(R13out), .in14(R14out),
    .in15(R15out), .in16(R16out), .in17(R17out), .in18(R18out), .in19(R19out), .in20(R20out), .in21(R21out),
    .in22(R22out), .in23(R23out), .in24(R24out), .in25(R25out), .in26(R26out), .in27(R27out), .in28(R28out),
    .in29(R29out), .in30(R30out), .in31(R31out), .out(outputRA), .sel(selectRA));
  // Probe on R17out
  // Probe on R19out
  // Probe on R21out
  // Probe on R23out
  // Probe on R25out
  // Probe on R27out
  // Probe on R29out
  // Probe on R31out
  // Probe on R2out
  // Probe on R10out
  // Probe on R18out
  Register #(.width(32)) register_11 (.D(inputRC), .en(enR18), .Q(R18out), .clk(clock), .clr(clear));
  // Probe on R26out
  Register #(.width(32)) register_12 (.D(inputRC), .en(enR26), .Q(R26out), .clk(clock), .clr(clear));
  // Probe on inputRC
  // Probe on inputRC
  // Probe on inputRC
  // Probe on inputRC
  // Probe on R3out
  Register #(.width(32)) register_13 (.D(inputRC), .en(enR3), .Q(R3out), .clk(clock), .clr(clear));
  // Probe on R11out
  Register #(.width(32)) register_14 (.D(inputRC), .en(enR11), .Q(R11out), .clk(clock), .clr(clear));
  // Probe on R19out
  Register #(.width(32)) register_15 (.D(inputRC), .en(enR19), .Q(R19out), .clk(clock), .clr(clear));
  // Probe on R27out
  Register #(.width(32)) register_16 (.D(inputRC), .en(enR27), .Q(R27out), .clk(clock), .clr(clear));
  Multiplexer #(.select(5), .width(32), .enable("false")) multiplexer_2 (
    .in0(R0out), .in1(R1out), .in2(R2out), .in3(R3out), .in4(R4out), .in5(R5out), .in6(R6out), .in7(R7out),
    .in8(R8out), .in9(R9out), .in10(R10out), .in11(R11out), .in12(R12out), .in13(R13out), .in14(R14out),
    .in15(R15out), .in16(R16out), .in17(R17out), .in18(R18out), .in19(R19out), .in20(R20out), .in21(R21out),
    .in22(R22out), .in23(R23out), .in24(R24out), .in25(R25out), .in26(R26out), .in27(R27out), .in28(R28out),
    .in29(R29out), .in30(R30out), .in31(R31out), .out(outputRB), .sel(selectRB));
  // Probe on inputRC
  // Probe on inputRC
  // Probe on inputRC
  // Probe on inputRC
  // Probe on R4out
  Register #(.width(32)) register_17 (.D(inputRC), .en(enR4), .Q(R4out), .clk(clock), .clr(clear));
  // Probe on R12out
  Register #(.width(32)) register_18 (.D(inputRC), .en(enR12), .Q(R12out), .clk(clock), .clr(clear));
  Register #(.width(32)) register_19 (.D(inputRC), .en(enR20), .Q(R20out), .clk(clock), .clr(clear));
  Register #(.width(32)) register_20 (.D(inputRC), .en(enR28), .Q(R28out), .clk(clock), .clr(clear));
  // Probe on R20out
  // Probe on R28out
  // Probe on inputRC
  Register #(.width(32)) register_21 (.D(inputRC), .en(enR5), .Q(R5out), .clk(clock), .clr(clear));
  // Probe on inputRC
  Register #(.width(32)) register_22 (.D(inputRC), .en(enR13), .Q(R13out), .clk(clock), .clr(clear));
  // Probe on inputRC
  // Probe on inputRC
  // Probe on R5out
  // Probe on R13out
  // Probe on R21out
  Register #(.width(32)) register_23 (.D(inputRC), .en(enR21), .Q(R21out), .clk(clock), .clr(clear));
  // Probe on R29out
  Register #(.width(32)) register_24 (.D(inputRC), .en(enR29), .Q(R29out), .clk(clock), .clr(clear));
  // Probe on inputRC
  // Probe on inputRC
  // Probe on inputRC
  // Probe on inputRC
  // Probe on R6out
  Register #(.width(32)) register_25 (.D(inputRC), .en(enR6), .Q(R6out), .clk(clock), .clr(clear));
  // Probe on R14out
  Register #(.width(32)) register_26 (.D(inputRC), .en(enR14), .Q(R14out), .clk(clock), .clr(clear));
  // Probe on R22out
  Register #(.width(32)) register_27 (.D(inputRC), .en(enR22), .Q(R22out), .clk(clock), .clr(clear));
  // Probe on R30out
  Register #(.width(32)) register_28 (.D(inputRC), .en(enR30), .Q(R30out), .clk(clock), .clr(clear));
  // Probe on inputRC
  // Probe on inputRC
  Register #(.width(32)) register_29 (.D(inputRC), .en(enR7), .Q(R7out), .clk(clock), .clr(clear));
  Register #(.width(32)) register_30 (.D(inputRC), .en(enR15), .Q(R15out), .clk(clock), .clr(clear));
  // Probe on inputRC
  Register #(.width(32)) register_31 (.D(inputRC), .en(enR23), .Q(R23out), .clk(clock), .clr(clear));
  // Probe on inputRC
  Register #(.width(32)) register_32 (.D(inputRC), .en(enR31), .Q(R31out), .clk(clock), .clr(clear));
  // Probe on R7out
  // Probe on R15out
  // Probe on R23out
  // Probe on R31out

  // Other names for the same wires on the sheet: clk = clock; clr = clear; RA[31:0] = outputRA; RB[31:0] = outputRB;
  //   Rin[31:0] = inputRC
endmodule

module ALU (
  input  [31:0] inA,
  input  [31:0] inB,
  input  [7:0] ALU_Control_In,
  output [1:0] ALU_Control_Out,
  output [31:0] out
);

  wire Bout, C, Cout, Greater, Z;
  wire [31:0] adder_1_out, and_1_out, divider_1_out, multiplier_1_out, negator_1_out, or_1_out,
       subtractor_1_out;

  Comparator #(.width(32), .mode("unsigned")) comparator_1 (.a(inA), .b(inB), .gt(Greater), .eq(Z));  // open: lt
  // Probe on C
  Multiplexer #(.select(4), .enable("false")) multiplexer_1 (
    .in1(Cout), .in2(Bout), .in3(Greater), .in4(Greater), .in5(Greater), .in6(Greater), .in7(Greater),
    .in8(Greater), .in9(Greater), .in10(Greater), .in11(Greater), .in12(Greater), .in13(Greater),
    .in14(Greater), .in15(Greater), .out(C), .sel(ALU_Control_In[6:3]));  // open: in0
  Register #(.width(1)) u_Cout (
    .D(C), .en(ALU_Control_In[7]), .Q(ALU_Control_Out[0]), .clk(ALU_Control_In[0]), .clr(ALU_Control_In[1]));
  Register #(.width(1)) Cout_2 (
    .D(Z), .en(ALU_Control_In[7]), .Q(ALU_Control_Out[1]), .clk(ALU_Control_In[0]), .clr(ALU_Control_In[1]));
  Adder #(.width(32)) adder_1 (.a(inA), .b(inB), .out(adder_1_out), .cin(ALU_Control_In[2]), .cout(Cout));
  Subtractor #(.width(32)) subtractor_1 (
    .a(inA), .b(inB), .out(subtractor_1_out), .bin(ALU_Control_In[2]), .bout(Bout));
  assign and_1_out = inA & inB;  // AND_Gate and_1, 32 bits wide
  assign or_1_out = inA | inB;  // OR_Gate or_1, 32 bits wide
  Negator #(.width(32)) negator_1 (.in(inB), .out(negator_1_out));
  Multiplier #(.width(32)) multiplier_1 (.a(inA), .b(inB), .out(multiplier_1_out));  // open: cin, cout
  Divider #(.width(32)) divider_1 (.a(inA), .b(inB), .out(divider_1_out));  // open: upper, rem
  Multiplexer #(.select(4), .width(32), .enable("false")) multiplexer_2 (
    .in0(inA), .in1(adder_1_out), .in2(subtractor_1_out), .in3(and_1_out), .in4(or_1_out),
    .in5(negator_1_out), .in6(multiplier_1_out), .in14(divider_1_out), .in15(inB), .out(out),
    .sel(ALU_Control_In[6:3]));  // open: in7, in8, in9, in10, in11, in12, in13
  // Probe on out

  // Other names for the same wires on the sheet: clk = ALU_Control_In[0]; clr = ALU_Control_In[1];
  //   Cin = ALU_Control_In[2]; enableFlag = ALU_Control_In[7]; selectALU[3:0] = ALU_Control_In[6:3]; zero = Z
endmodule

// Control Unit
module CU (
  input  [31:0] IR,
  input  Clear,
  input  [1:0] ALU_Control_Out,
  output CPU_Halt,
  output [31:0] Immediate,
  output Clock,
  output [31:0] Output_Signals,
  output [7:0] ALU_Control
);

  wire add, \and , and_1_out, and_4_out, and_5_out, and_6_out, and_7_out, and_8_out, clock_t, compare,
       d_ff_1_qn, halt, jc, jump, jz, load, move, nop, \not , \or , or_1_out, or_3_out, or_4_out, or_5_out,
       or_7_out, or_9_out, rnd, stage3, stage4, stage5, store, subtract, \xor ;
  wire [2:0] Counter_q;

  Clock clock_1 (.out(clock_t));
  or or_1 (or_1_out, CPU_Halt, and_1_out);
  and and_1 (and_1_out, halt, stage5);
  Multiplexer #(.select(5), .width(4), .enable("false")) multiplexer_1 (
    .in0(4'b0000), .in1(4'b1111), .in2(4'b0000), .in3(4'b1111), .in4(4'b1111), .in5(4'b1111), .in6(4'b1111),
    .in7(4'b0000), .in8(4'b0001), .in9(4'b0010), .in10(4'b0011), .in11(4'b0100), .in12(4'b0101),
    .in13(4'b0110), .in14(4'b1110), .in15(4'b1101), .in16(4'b0000), .in17(4'b0000), .in18(4'b0000),
    .in19(4'b0000), .in20(4'b0000), .in21(4'b0000), .in22(4'b0000), .in23(4'b0000), .in24(4'b0000),
    .in25(4'b0000), .in26(4'b0000), .in27(4'b0000), .in28(4'b0000), .in29(4'b0000), .in30(4'b0000),
    .in31(4'b0000), .out(ALU_Control[6:3]), .sel(IR[31:27]));
  D_Flip_Flop d_ff_1 (.clk(clock_t), .D(or_1_out), .Q(CPU_Halt), .Qn(d_ff_1_qn), .reset(Clear));  // open: preset, en
  and and_2 (ALU_Control[0], d_ff_1_qn, clock_t);
  or or_2 (Output_Signals[16], load, store);
  or or_3 (or_3_out, move, add, subtract, \and , load, \not , \or , rnd, \xor );
  Decoder #(.select(3), .enable("false")) decoder_1 (
    .out0(Output_Signals[7]), .out1(Output_Signals[5]), .out2(stage3), .out3(stage4), .out4(stage5),
    .sel(Counter_q));  // open: out5, out6, out7
  Counter #(.width(3), .max('h4)) Counter (
    .Q(Counter_q), .clk(ALU_Control[0]), .clr(Clear));  // open: load, D, count, carry
  and and_3 (Output_Signals[6], stage5, or_3_out);
  Decoder #(.select(5), .enable("false")) decoder_2 (
    .out0(halt), .out1(load), .out2(store), .out3(move), .out4(jump), .out5(jz), .out6(jc), .out7(nop),
    .out8(add), .out9(subtract), .out10(\and ), .out11(\or ), .out12(\not ), .out13(\xor ), .out14(rnd),
    .out15(compare), .out16(nop), .out17(nop), .out18(nop), .out19(nop), .out20(nop), .out21(nop),
    .out22(nop), .out23(nop), .out24(nop), .out25(nop), .out26(nop), .out27(nop), .out28(nop), .out29(nop),
    .out30(nop), .out31(nop), .sel(IR[31:27]));
  and and_4 (and_4_out, jz, ALU_Control_Out[1]);
  and and_5 (and_5_out, jc, ALU_Control_Out[0]);
  or or_4 (or_4_out, load, store);
  and and_6 (and_6_out, stage4, load);
  or or_5 (or_5_out, and_4_out, and_5_out, jump);
  and and_7 (and_7_out, or_5_out, stage4);
  or or_6 (Output_Signals[0], Output_Signals[7], and_8_out);
  and and_8 (and_8_out, stage4, or_4_out);
  or or_7 (or_7_out, subtract, add, compare);
  or or_8 (Output_Signals[1], Output_Signals[7], and_6_out);
  or or_9 (or_9_out, and_7_out, Output_Signals[5]);
  and and_9 (Output_Signals[8], or_9_out, ~halt);  // AND_Gate
  and and_10 (ALU_Control[7], stage3, or_7_out);

  assign ALU_Control[2:1] = {1'b0, Clear};
  assign Clock = ALU_Control[0];
  assign Immediate = {{16{1'b0}}, IR[16:1]};
  assign {Output_Signals[31:17], Output_Signals[4:2]} = {IR[21:12], IR[26:22], Output_Signals[5], IR[0], Output_Signals[7]};

  // Other names for the same wires on the sheet: op5 = IR[27]; op4 = IR[28]; op3 = IR[29]; op2 = IR[30]; op1 = IR[31];
  //   clk = ALU_Control[0]; clr = Clear; enableFlag = ALU_Control[7]; C = ALU_Control_Out[0]; Z = ALU_Control_Out[1];
  //   D11 = IR[1]; D10 = IR[2]; D9 = IR[3]; D8 = IR[4]; D7 = IR[5]; D6 = IR[6]; D5 = IR[7]; D4 = IR[8]; D3 = IR[9];
  //   D2 = IR[10]; D1 = IR[11]; B5 = IR[12]; selectRB[4:0] = IR[16:12]; B4 = IR[13]; B3 = IR[14]; B2 = IR[15];
  //   B1 = IR[16]; enImmediate = IR[0]; selectMuxB = IR[0]; memEnable = Output_Signals[0];
  //   memLoadStore = Output_Signals[1]; selectMuxINC = Output_Signals[5]; selectMuxPC = Output_Signals[5];
  //   stage2 = Output_Signals[5]; enRWrite = Output_Signals[6]; enableIR = Output_Signals[7];
  //   selectMuxA = Output_Signals[7]; stage1 = Output_Signals[7]; enPC = Output_Signals[8];
  //   selectMuxY = Output_Signals[16]; selectALU[3:0] = ALU_Control[6:3]; A5 = IR[22]; selectRA[4:0] = IR[26:22];
  //   A4 = IR[23]; A3 = IR[24]; A2 = IR[25]; A1 = IR[26]; C5 = IR[17]; selectRC[4:0] = IR[21:17]; C4 = IR[18];
  //   C3 = IR[19]; C2 = IR[20]; C1 = IR[21]
endmodule

module format (
);

  wire undriven, undriven_2, undriven_3, undriven_4, undriven_5;
  wire [31:0] Dummy_Instruction_Format_32_Bit_q31;

  Shift_Register #(.length(32)) Dummy_Instruction_Format_32_Bit (
    .clk(1'b1), .d0(undriven), .q0(Dummy_Instruction_Format_32_Bit_q31[31]),
    .q1(Dummy_Instruction_Format_32_Bit_q31[30]), .q2(Dummy_Instruction_Format_32_Bit_q31[29]),
    .q3(Dummy_Instruction_Format_32_Bit_q31[28]), .d4(undriven),
    .q4(Dummy_Instruction_Format_32_Bit_q31[27]), .d5(undriven_2),
    .q5(Dummy_Instruction_Format_32_Bit_q31[26]), .q6(Dummy_Instruction_Format_32_Bit_q31[25]),
    .q7(Dummy_Instruction_Format_32_Bit_q31[24]), .q8(Dummy_Instruction_Format_32_Bit_q31[23]),
    .d9(undriven_2), .q9(Dummy_Instruction_Format_32_Bit_q31[22]), .d10(undriven_3),
    .q10(Dummy_Instruction_Format_32_Bit_q31[21]), .q11(Dummy_Instruction_Format_32_Bit_q31[20]),
    .q12(Dummy_Instruction_Format_32_Bit_q31[19]), .q13(Dummy_Instruction_Format_32_Bit_q31[18]),
    .d14(undriven_3), .q14(Dummy_Instruction_Format_32_Bit_q31[17]), .d15(undriven_4),
    .q15(Dummy_Instruction_Format_32_Bit_q31[16]), .q16(Dummy_Instruction_Format_32_Bit_q31[15]),
    .q17(Dummy_Instruction_Format_32_Bit_q31[14]), .q18(Dummy_Instruction_Format_32_Bit_q31[13]),
    .d19(undriven_4), .q19(Dummy_Instruction_Format_32_Bit_q31[12]),
    .q20(Dummy_Instruction_Format_32_Bit_q31[11]), .q21(Dummy_Instruction_Format_32_Bit_q31[10]),
    .q22(Dummy_Instruction_Format_32_Bit_q31[9]), .q23(Dummy_Instruction_Format_32_Bit_q31[8]),
    .q24(Dummy_Instruction_Format_32_Bit_q31[7]), .q25(Dummy_Instruction_Format_32_Bit_q31[6]),
    .q26(Dummy_Instruction_Format_32_Bit_q31[5]), .q27(Dummy_Instruction_Format_32_Bit_q31[4]),
    .q28(Dummy_Instruction_Format_32_Bit_q31[3]), .q29(Dummy_Instruction_Format_32_Bit_q31[2]),
    .d30(undriven_4), .q30(Dummy_Instruction_Format_32_Bit_q31[1]), .d31(undriven_5),
    .q31(Dummy_Instruction_Format_32_Bit_q31[0]));  // open: shift, in, out, load, clr, d1, d2, d3, d6, d7, d8, d11, d12, d13, d16, d17, d18, d20, d21, d22, d23, d24, d25, d26, d27, d28, d29
  // Probe on Dummy_Instruction_Format_32_Bit_q31

  // Notes on the sheet:
  //   OpCode
  //   RA
  //   RC
  //   Immediate(16 Bit)
  //   RB
  //   enableImmediate
endmodule
